# Fritzing sketch battery_analog_checker_sketch (saved by Fritzing 0.9.3b)
breadboards: 1

parts:
  R1 = Resistor [tolerance=±5% resistance=10k package=THT]
  Arduino_Uno = Arduino Uno (Rev3)
  B1 = Battery Holders [package=battery-aa]
  R2 = Resistor [tolerance=±5% resistance=10k package=THT]

nets:
  N1: R1.Pin_0, Arduino_Uno.GND, B1.-
  N2: R1.Pin_1, Arduino_Uno.A0, R2.Pin_0
  N3: B1.+, R2.Pin_1
